# Fritzing sketch Morse_Receiver_Scheme (saved by Fritzing 0.9.4)
breadboards: 1

parts:
  part = Arduino Uno (Rev3)
  R1 = PHOTOCELL [package=photocell-kit]
  R2 = Resistor [tolerance=±5% resistance=10k package="1206 [SMD]"]
  Grove1 = Grove OLED 128x96

nets:
  GND: part.GND, R2.Pin_0, Grove1.GND
  N1: part.A4/SDA, Grove1.SCL
  N2: part.A5/SCL, Grove1.SDA
  5V: part.5V, R1.P$1, Grove1.VCC
  N3: R1.P$2, R2.Pin_1
