# Fritzing sketch Morse_Transmitter_Scheme (saved by Fritzing 0.9.4)
breadboards: 1

parts:
  Компонент1 = Arduino Uno (Rev3)
  R1 = Rotary Potentiometer (Small) [maximum_resistance=100kΩ package=THT]
  LED1 = RGB LED (com. cathode, rgb) [package="5 mm [THT]"]
  J1 = Piezo Speaker
  Grove1 = Grove OLED 128x96
  HC-SR04_Sensor_1 = HC-SR04 Ultrasonic Distance Sensor
  LED2 = DUO LED RG [package="5 mm [THT]"]
  R2 = Resistor [tolerance=±5% resistance=220 package="0805 [SMD]"]
  R3 = Resistor [tolerance=±5% resistance=220 package="0805 [SMD]"]
  R5 = Resistor [tolerance=±5% resistance=220 package="0805 [SMD]"]

nets:
  N1: Компонент1.A0, R1.wiper
  N2: Компонент1.A4/SDA, Grove1.SDA
  N3: Компонент1.D8, R3.Pin_0
  N4: Компонент1.D11_PWM/MOSI, HC-SR04_Sensor_1.GND
  N5: Компонент1.D12/MISO, HC-SR04_Sensor_1.TRIG
  GND: Компонент1.GND, R1.leg1, LED1.common_cathode, J1.pin2, Grove1.GND, HC-SR04_Sensor_1.ECHO, LED2.common_cathode
  N6: Компонент1.A5/SCL, Grove1.SCL
  N7: Компонент1.D3_PWM, J1.pin1
  N8: Компонент1.D5_PWM, R5.Pin_0
  N9: Компонент1.D6_PWM, R2.Pin_0
  VCC: Компонент1.5V, R1.leg2, Grove1.VCC, HC-SR04_Sensor_1.VCC
  N10: LED1.red_anode, R5.Pin_1
  N11: LED1.green_anode, R2.Pin_1
  N12: LED2.green_anode, R3.Pin_1
